// Logisim project ALU.circ as structural Verilog: 1 circuit, main circuit main
module main (
  input  Sub_Carry_In,
  input  [7:0] B,
  input  [7:0] A,
  input  Carry_In,
  input  A_2,
  input  B_2,
  input  Ci_Sub,
  input  A_3,
  input  Ci,
  input  B_3,
  input  A_4,
  input  B_4,
  input  [2:0] OP,
  input  [2:0] OP_2,
  input  [3:0] B_5,
  input  [3:0] A_5,
  input  CERO,
  input  [2:0] OP_3,
  input  Ci_2,
  input  A0,
  input  B0,
  input  Ci_Sub_2,
  input  [2:0] OP_4,
  input  [7:0] A_6,
  input  [7:0] B_6,
  input  in_26,
  input  [31:0] A_7,
  input  A1,
  input  B1,
  input  [31:0] B_7,
  input  A2,
  input  B2,
  input  A3,
  input  B3,
  input  A4,
  input  B4,
  input  A5,
  input  B5,
  input  A6,
  input  B6,
  input  A7,
  input  B7,
  input  A8,
  input  B8,
  output [7:0] out_45,
  output Salida,
  output Carry_Out,
  output S,
  output S_2,
  output Ci_1,
  output Ci_1_2,
  output Carry_out_2,
  output S0,
  output [7:0] Salida_2,
  output [7:0] SALIDA_3,
  output [31:0] out_56,
  output S1,
  output out_58,
  output S2,
  output S3,
  output S4,
  output S5,
  output S6,
  output Ci_1_3,
  output S7,
  output S8,
  output Desbordamiento
);

  wire adder_1_cout, and_1_out, and_2_out, and_3_out, and_4_out, and_5_out, and_6_out, and_7_out, and_8_out,
       and_9_out, and_10_out, and_11_out, and_12_out, and_13_out, and_14_out, and_15_out, and_16_out,
       and_17_out, and_18_out, and_19_out, and_20_out, and_21_out, and_22_out, and_23_out, and_24_out,
       and_25_out, and_26_out, and_27_out, and_28_out, and_29_out, and_30_out, and_31_out, and_32_out,
       and_33_out, and_34_out, and_35_out, and_36_out, and_37_out, and_38_out, and_39_out, and_40_out,
       and_41_out, and_42_out, and_43_out, and_44_out, and_45_out, and_46_out, and_47_out, and_48_out,
       and_49_out, and_50_out, and_51_out, and_52_out, and_53_out, and_54_out, and_55_out, and_56_out,
       and_57_out, and_58_out, and_59_out, and_60_out, and_61_out, and_62_out, and_63_out, and_64_out,
       and_65_out, and_66_out, and_67_out, and_68_out, and_69_out, and_70_out, and_71_out, and_72_out,
       and_73_out, and_74_out, and_75_out, and_76_out, and_77_out, and_78_out, and_79_out, and_80_out,
       and_81_out, and_82_out, and_83_out, and_84_out, and_85_out, and_86_out, and_87_out, and_88_out,
       and_89_out, and_90_out, and_91_out, and_92_out, and_93_out, and_94_out, and_95_out, and_96_out,
       and_97_out, and_98_out, and_99_out, and_100_out, and_101_out, and_102_out, and_103_out, and_104_out,
       and_105_out, and_106_out, and_107_out, and_108_out, and_109_out, and_110_out, and_111_out,
       and_112_out, and_113_out, and_114_out, and_115_out, and_116_out, and_117_out, and_118_out,
       and_119_out, and_120_out, and_121_out, and_122_out, and_123_out, and_124_out, and_125_out,
       and_126_out, and_127_out, and_128_out, and_129_out, and_130_out, and_131_out, and_132_out,
       and_133_out, and_134_out, and_135_out, and_136_out, and_137_out, not_1_out, not_2_out, not_3_out,
       not_4_out, not_5_out, not_6_out, not_7_out, not_8_out, not_9_out, not_10_out, not_11_out, not_12_out,
       not_13_out, not_14_out, not_15_out, not_16_out, not_17_out, not_18_out, not_19_out, not_20_out,
       not_21_out, not_22_out, not_23_out, not_24_out, not_25_out, not_26_out, not_27_out, not_28_out,
       not_29_out, not_30_out, not_31_out, not_32_out, not_33_out, not_34_out, not_35_out, not_36_out,
       not_37_out, not_38_out, not_39_out, not_40_out, not_41_out, not_42_out, not_43_out, not_44_out,
       not_45_out, not_46_out, not_47_out, not_48_out, not_49_out, not_50_out, not_51_out, not_52_out,
       not_53_out, not_54_out, not_55_out, not_56_out, not_57_out, not_58_out, not_59_out, not_60_out,
       not_61_out, not_62_out, not_63_out, not_64_out, not_65_out, not_66_out, not_67_out, not_68_out,
       not_69_out, not_70_out, not_71_out, not_72_out, not_73_out, not_74_out, not_75_out, not_76_out,
       not_77_out, not_78_out, not_79_out, not_80_out, not_81_out, not_82_out, not_83_out, not_84_out,
       not_85_out, not_86_out, not_87_out, not_88_out, or_1_out, or_2_out, or_3_out, or_4_out, or_5_out,
       or_6_out, or_7_out, or_8_out, or_9_out, or_10_out, or_11_out, or_12_out, or_13_out, or_14_out,
       or_16_out, or_17_out, or_18_out, or_19_out, or_20_out, or_21_out, or_22_out, or_23_out, or_24_out,
       or_25_out, or_26_out, or_27_out, or_30_out, or_31_out, or_32_out, or_33_out, or_34_out, or_35_out,
       or_36_out, or_37_out, or_38_out, or_39_out, or_41_out, or_42_out, or_44_out, or_45_out, or_46_out,
       or_47_out, or_48_out, or_49_out, or_50_out, or_52_out, or_53_out, or_54_out, or_55_out, or_56_out,
       or_57_out, or_58_out, or_59_out, or_60_out, or_61_out, or_62_out, or_63_out, or_64_out, or_65_out,
       or_66_out, or_68_out, undriven, undriven_2, xor_1_out, xor_2_out, xor_3_out, xor_5_out, xor_6_out,
       xor_7_out, xor_8_out, xor_9_out, xor_10_out, xor_11_out, xor_12_out, xor_13_out, xor_14_out,
       xor_15_out, xor_16_out, xor_17_out, xor_18_out, xor_19_out, xor_20_out, xor_21_out, xor_22_out,
       xor_23_out, xor_24_out, xor_25_out, xor_26_out, xor_27_out, xor_28_out, xor_37_out, xor_38_out,
       xor_39_out, xor_40_out, xor_41_out, xor_42_out, xor_43_out, xor_44_out, xor_45_out, xor_46_out,
       xor_47_out, xor_48_out, xor_49_out, xor_50_out, xor_51_out, xor_52_out, xor_53_out, xor_54_out,
       xor_55_out, xor_56_out, xor_57_out, xor_58_out, xor_59_out, xor_60_out, xor_61_out, xor_62_out,
       xor_63_out, xor_64_out;
  wire [3:0] adder_3_cout, adder_4_cout, and_141_out, and_145_out, and_149_out;
  wire [3:1] and_152_out;

  not not_1 (not_1_out, B_4);
  not not_2 (not_2_out, A_4);
  not not_3 (not_3_out, B6);
  not not_4 (not_4_out, A6);
  not not_5 (not_5_out, B7);
  not not_6 (not_6_out, A7);
  not not_7 (not_7_out, B8);
  not not_8 (not_8_out, A8);
  and and_1 (and_1_out, A_4, not_1_out);
  and and_2 (and_2_out, not_2_out, B_4);
  not not_9 (not_9_out, B0);
  not not_10 (not_10_out, A0);
  not not_11 (not_11_out, B1);
  not not_12 (not_12_out, A1);
  not not_13 (not_13_out, B2);
  not not_14 (not_14_out, A2);
  and and_3 (and_3_out, A3, not_15_out);
  not not_15 (not_15_out, B3);
  not not_16 (not_16_out, A3);
  not not_17 (not_17_out, B4);
  not not_18 (not_18_out, A4);
  and and_4 (and_4_out, A5, not_19_out);
  not not_19 (not_19_out, B5);
  not not_20 (not_20_out, A5);
  and and_5 (and_5_out, A6, not_3_out);
  and and_6 (and_6_out, not_4_out, B6);
  and and_7 (and_7_out, A7, not_5_out);
  and and_8 (and_8_out, not_6_out, B7);
  and and_9 (and_9_out, A8, not_7_out);
  and and_10 (and_10_out, not_8_out, B8);
  and and_11 (and_11_out, A8, B8);
  or or_1 (or_1_out, and_1_out, and_2_out);
  and and_12 (and_12_out, A_4, B_4);
  and and_13 (and_13_out, A0, not_9_out);
  and and_14 (and_14_out, not_10_out, B0);
  and and_15 (and_15_out, A1, not_11_out);
  and and_16 (and_16_out, not_12_out, B1);
  and and_17 (and_17_out, A2, not_13_out);
  and and_18 (and_18_out, not_14_out, B2);
  and and_19 (and_19_out, A2, B2);
  and and_20 (and_20_out, not_16_out, B3);
  and and_21 (and_21_out, A3, B3);
  and and_22 (and_22_out, A4, not_17_out);
  and and_23 (and_23_out, not_18_out, B4);
  and and_24 (and_24_out, A4, B4);
  and and_25 (and_25_out, not_20_out, B5);
  and and_26 (and_26_out, A5, B5);
  or or_2 (or_2_out, and_5_out, and_6_out);
  and and_27 (and_27_out, A6, B6);
  or or_3 (or_3_out, and_7_out, and_8_out);
  and and_28 (and_28_out, A7, B7);
  or or_4 (or_4_out, and_9_out, and_10_out);
  // XOR_Gate xor_1 has open pins: out=xor_1_out
  and and_29 (and_29_out, undriven, undriven);
  or or_5 (or_5_out, and_13_out, and_14_out);
  and and_30 (and_30_out, A0, B0);
  or or_6 (or_6_out, and_15_out, and_16_out);
  and and_31 (and_31_out, A1, B1);
  or or_7 (or_7_out, and_17_out, and_18_out);
  or or_8 (or_8_out, and_3_out, and_20_out);
  or or_9 (or_9_out, and_22_out, and_23_out);
  or or_10 (or_10_out, and_4_out, and_25_out);
  and and_32 (and_32_out, xor_1_out, undriven_2);
  and and_33 (and_33_out, A_4, B_4);
  or or_11 (or_11_out, A_4, B_4);
  not not_21 (not_21_out, A_4);
  not not_22 (not_22_out, Ci);
  not not_23 (not_23_out, or_1_out);
  not not_24 (not_24_out, A3);
  not not_25 (not_25_out, or_33_out);
  not not_26 (not_26_out, or_8_out);
  not not_27 (not_27_out, A5);
  not not_28 (not_28_out, or_36_out);
  not not_29 (not_29_out, or_10_out);
  and and_34 (and_34_out, A6, B6);
  or or_12 (or_12_out, A6, B6);
  not not_30 (not_30_out, A6);
  not not_31 (not_31_out, or_37_out);
  not not_32 (not_32_out, or_2_out);
  and and_35 (and_35_out, A7, B7);
  or or_13 (or_13_out, A7, B7);
  not not_33 (not_33_out, A7);
  not not_34 (not_34_out, or_38_out);
  not not_35 (not_35_out, or_3_out);
  and and_36 (and_36_out, A8, B8);
  or or_14 (or_14_out, A8, B8);
  not not_36 (not_36_out, A8);
  and and_37 (and_37_out, or_4_out, not_37_out);
  not not_37 (not_37_out, or_39_out);
  not not_38 (not_38_out, or_4_out);
  xor xor_2 (xor_2_out, xor_1_out, undriven_2);
  // OR_Gate or_15 has open pins: in1=and_32_out, in4=and_29_out, out=open
  and and_38 (and_38_out, or_1_out, not_22_out);
  and and_39 (and_39_out, not_23_out, Ci);
  and and_40 (and_40_out, or_1_out, Ci);
  and and_41 (and_41_out, A0, B0);
  or or_16 (or_16_out, A0, B0);
  not not_39 (not_39_out, A0);
  not not_40 (not_40_out, Ci_2);
  not not_41 (not_41_out, or_5_out);
  and and_42 (and_42_out, A1, B1);
  or or_17 (or_17_out, A1, B1);
  not not_42 (not_42_out, A1);
  not not_43 (not_43_out, or_41_out);
  not not_44 (not_44_out, or_6_out);
  and and_43 (and_43_out, A2, B2);
  or or_18 (or_18_out, A2, B2);
  not not_45 (not_45_out, A2);
  and and_44 (and_44_out, or_7_out, not_46_out);
  not not_46 (not_46_out, or_42_out);
  not not_47 (not_47_out, or_7_out);
  and and_45 (and_45_out, A3, B3);
  or or_19 (or_19_out, A3, B3);
  and and_46 (and_46_out, or_8_out, not_25_out);
  and and_47 (and_47_out, not_26_out, or_33_out);
  and and_48 (and_48_out, A4, B4);
  or or_20 (or_20_out, A4, B4);
  not not_48 (not_48_out, A4);
  and and_49 (and_49_out, or_9_out, not_49_out);
  not not_49 (not_49_out, or_34_out);
  not not_50 (not_50_out, or_9_out);
  and and_50 (and_50_out, A5, B5);
  or or_21 (or_21_out, A5, B5);
  and and_51 (and_51_out, or_10_out, not_28_out);
  and and_52 (and_52_out, not_29_out, or_36_out);
  and and_53 (and_53_out, or_2_out, not_31_out);
  and and_54 (and_54_out, not_32_out, or_37_out);
  and and_55 (and_55_out, or_2_out, or_37_out);
  and and_56 (and_56_out, or_3_out, not_34_out);
  and and_57 (and_57_out, not_35_out, or_38_out);
  and and_58 (and_58_out, or_3_out, or_38_out);
  and and_59 (and_59_out, not_38_out, or_39_out);
  and and_60 (and_60_out, or_4_out, or_39_out);
  // NOT_Gate not_51 has open pins: in=open, out=not_51_out
  // NOT_Gate not_52 has open pins: in=open, out=not_52_out
  or or_22 (or_22_out, and_38_out, and_39_out);
  and and_61 (and_61_out, or_5_out, not_40_out);
  and and_62 (and_62_out, not_41_out, Ci_2);
  and and_63 (and_63_out, or_6_out, not_43_out);
  and and_64 (and_64_out, not_44_out, or_41_out);
  and and_65 (and_65_out, or_6_out, or_41_out);
  and and_66 (and_66_out, not_47_out, or_42_out);
  and and_67 (and_67_out, or_7_out, or_42_out);
  or or_23 (or_23_out, and_46_out, and_47_out);
  and and_68 (and_68_out, or_8_out, or_33_out);
  and and_69 (and_69_out, not_50_out, or_34_out);
  and and_70 (and_70_out, or_9_out, or_34_out);
  or or_24 (or_24_out, and_51_out, and_52_out);
  and and_71 (and_71_out, or_10_out, or_36_out);
  or or_25 (or_25_out, and_53_out, and_54_out);
  or or_26 (or_26_out, and_56_out, and_57_out);
  or or_27 (or_27_out, and_37_out, and_59_out);
  or or_28 (Desbordamiento, and_60_out, and_11_out);
  buf and_72 (and_72_out, not_51_out);  // AND_Gate
  or or_29 (Ci_1_2, and_40_out, and_12_out);
  or or_30 (or_30_out, and_61_out, and_62_out);
  and and_73 (and_73_out, or_5_out, Ci_2);
  or or_31 (or_31_out, and_63_out, and_64_out);
  or or_32 (or_32_out, and_44_out, and_66_out);
  or or_33 (or_33_out, and_67_out, and_19_out);
  or or_34 (or_34_out, and_68_out, and_21_out);
  or or_35 (or_35_out, and_49_out, and_69_out);
  or or_36 (or_36_out, and_70_out, and_24_out);
  or or_37 (or_37_out, and_71_out, and_26_out);
  or or_38 (or_38_out, and_55_out, and_27_out);
  or or_39 (or_39_out, and_58_out, and_28_out);
  // OR_Gate or_40 has open pins: in1=and_72_out, in3=and_74_out, out=open
  buf and_74 (and_74_out, not_52_out);  // AND_Gate
  Multiplexer #(.select(3)) multiplexer_1 (
    .in0(and_33_out), .in1(or_11_out), .in2(not_21_out), .in3(or_22_out), .out(S_2), .sel(OP_2));  // open: in4, in5, in6, in7, en
  or or_41 (or_41_out, and_73_out, and_30_out);
  or or_42 (or_42_out, and_65_out, and_31_out);
  Multiplexer #(.select(3)) multiplexer_2 (
    .in0(and_34_out), .in1(or_12_out), .in2(not_30_out), .in3(or_25_out), .out(S6), .sel(OP_3));  // open: in4, in5, in6, in7, en
  Multiplexer #(.select(3)) multiplexer_3 (
    .in0(and_35_out), .in1(or_13_out), .in2(not_33_out), .in3(or_26_out), .out(S7), .sel(OP_3));  // open: in4, in5, in6, in7, en
  Multiplexer #(.select(3)) multiplexer_4 (
    .in0(and_36_out), .in1(or_14_out), .in2(not_36_out), .in3(or_27_out), .out(S8), .sel(OP_3));  // open: in4, in5, in6, in7, en
  Multiplexer #(.select(3)) multiplexer_5 (
    .in0(and_41_out), .in1(or_16_out), .in2(not_39_out), .in3(or_30_out), .out(S0), .sel(OP_3));  // open: in4, in5, in6, in7, en
  Multiplexer #(.select(3)) multiplexer_6 (
    .in0(and_42_out), .in1(or_17_out), .in2(not_42_out), .in3(or_31_out), .out(S1), .sel(OP_3));  // open: in4, in5, in6, in7, en
  Multiplexer #(.select(3)) multiplexer_7 (
    .in0(and_43_out), .in1(or_18_out), .in2(not_45_out), .in3(or_32_out), .out(S2), .sel(OP_3));  // open: in4, in5, in6, in7, en
  Multiplexer #(.select(3)) multiplexer_8 (
    .in0(and_45_out), .in1(or_19_out), .in2(not_24_out), .in3(or_23_out), .out(S3), .sel(OP_3));  // open: in4, in5, in6, in7, en
  Multiplexer #(.select(3)) multiplexer_9 (
    .in0(and_48_out), .in1(or_20_out), .in2(not_48_out), .in3(or_35_out), .out(S4), .sel(OP_3));  // open: in4, in5, in6, in7, en
  Multiplexer #(.select(3)) multiplexer_10 (
    .in0(and_50_out), .in1(or_21_out), .in2(not_27_out), .in3(or_24_out), .out(S5), .sel(OP_3));  // open: in4, in5, in6, in7, en
  and and_75 (and_75_out, A_2, B_2, B_2);
  xor xor_3 (xor_3_out, A_2, B_2);
  xor xor_4 (Salida, xor_3_out, Carry_In);
  and and_76 (and_76_out, xor_3_out, Carry_In);
  or or_43 (Carry_Out, and_76_out, and_75_out);
  xor xor_5 (xor_5_out, Sub_Carry_In, B[6]);
  buf xor_6 (xor_6_out, Sub_Carry_In);  // XOR_Gate
  xor xor_7 (xor_7_out, Sub_Carry_In, B[1]);
  xor xor_8 (xor_8_out, B[2], Sub_Carry_In);
  xor xor_9 (xor_9_out, Sub_Carry_In, B[3]);
  xor xor_10 (xor_10_out, Sub_Carry_In, B[4]);
  xor xor_11 (xor_11_out, Sub_Carry_In, B[5]);
  xor xor_12 (xor_12_out, Sub_Carry_In, B[7]);
  xor xor_13 (xor_13_out, A[0], xor_6_out);
  and and_77 (and_77_out, A[0], xor_6_out);
  xor xor_14 (xor_14_out, A[1], xor_7_out);
  and and_78 (and_78_out, A[1], xor_7_out);
  xor xor_15 (xor_15_out, A[2], xor_8_out);
  and and_79 (and_79_out, A[2], xor_8_out);
  xor xor_16 (xor_16_out, A[3], xor_9_out);
  and and_80 (and_80_out, A[3], xor_9_out);
  xor xor_17 (xor_17_out, A[4], xor_10_out);
  and and_81 (and_81_out, A[4], xor_10_out);
  xor xor_18 (xor_18_out, A[5], xor_11_out);
  and and_82 (and_82_out, A[5], xor_11_out);
  xor xor_19 (xor_19_out, A[6], xor_5_out);
  and and_83 (and_83_out, A[6], xor_5_out);
  xor xor_20 (xor_20_out, A[7], xor_12_out);
  and and_84 (and_84_out, A[7], xor_12_out);
  xor xor_21 (xor_21_out, Ci_Sub_2, B_6[4]);
  xor xor_22 (xor_22_out, Ci_Sub_2, B_6[5]);
  xor xor_23 (xor_23_out, Ci_Sub_2, B_6[6]);
  and and_85 (and_85_out, xor_13_out, Sub_Carry_In);
  and and_86 (and_86_out, xor_14_out, or_44_out);
  and and_87 (and_87_out, xor_15_out, or_45_out);
  and and_88 (and_88_out, xor_16_out, or_46_out);
  and and_89 (and_89_out, xor_17_out, or_47_out);
  and and_90 (and_90_out, xor_18_out, or_48_out);
  and and_91 (and_91_out, xor_19_out, or_49_out);
  and and_92 (and_92_out, xor_20_out, or_50_out);
  xor xor_24 (xor_24_out, Ci_Sub_2, B_6[0]);
  xor xor_25 (xor_25_out, Ci_Sub_2, B_6[1]);
  xor xor_26 (xor_26_out, Ci_Sub_2, B_6[2]);
  xor xor_27 (xor_27_out, Ci_Sub_2, B_6[3]);
  xor xor_28 (xor_28_out, Ci_Sub_2, B_6[7]);
  xor xor_29 (out_45[0], xor_13_out, Sub_Carry_In);
  or or_44 (or_44_out, and_85_out, and_77_out);
  xor xor_30 (out_45[1], xor_14_out, or_44_out);
  or or_45 (or_45_out, and_86_out, and_78_out);
  xor xor_31 (out_45[2], xor_15_out, or_45_out);
  or or_46 (or_46_out, and_87_out, and_79_out);
  xor xor_32 (out_45[3], xor_16_out, or_46_out);
  or or_47 (or_47_out, and_88_out, and_80_out);
  xor xor_33 (out_45[4], xor_17_out, or_47_out);
  or or_48 (or_48_out, and_89_out, and_81_out);
  xor xor_34 (out_45[5], xor_18_out, or_48_out);
  or or_49 (or_49_out, and_90_out, and_82_out);
  xor xor_35 (out_45[6], xor_19_out, or_49_out);
  or or_50 (or_50_out, and_91_out, and_83_out);
  xor xor_36 (out_45[7], xor_20_out, or_50_out);
  or or_51 (Carry_out_2, and_92_out, and_84_out);
  xor xor_37 (xor_37_out, A_6[0], xor_24_out);
  and and_93 (and_93_out, A_6[0], xor_24_out, xor_24_out);
  xor xor_38 (xor_38_out, A_6[1], xor_25_out);
  and and_94 (and_94_out, A_6[1], xor_25_out, xor_25_out);
  xor xor_39 (xor_39_out, A_6[2], xor_26_out);
  and and_95 (and_95_out, A_6[2], xor_26_out, xor_26_out);
  xor xor_40 (xor_40_out, A_6[3], xor_27_out);
  and and_96 (and_96_out, A_6[3], xor_27_out, xor_27_out);
  xor xor_41 (xor_41_out, A_6[4], xor_21_out);
  and and_97 (and_97_out, A_6[4], xor_21_out, xor_21_out);
  xor xor_42 (xor_42_out, A_6[5], xor_22_out);
  and and_98 (and_98_out, A_6[5], xor_22_out, xor_22_out);
  xor xor_43 (xor_43_out, A_6[6], xor_23_out);
  and and_99 (and_99_out, A_6[6], xor_23_out, xor_23_out);
  xor xor_44 (xor_44_out, A_6[7], xor_28_out);
  and and_100 (and_100_out, A_6[7], xor_28_out, xor_28_out);
  not not_53 (not_53_out, A_6[0]);
  and and_101 (and_101_out, xor_37_out, Ci_Sub_2);
  not not_54 (not_54_out, A_6[1]);
  and and_102 (and_102_out, xor_38_out, or_63_out);
  not not_55 (not_55_out, A_6[2]);
  and and_103 (and_103_out, xor_39_out, or_64_out);
  not not_56 (not_56_out, A_6[3]);
  and and_104 (and_104_out, xor_40_out, or_65_out);
  not not_57 (not_57_out, A_6[4]);
  and and_105 (and_105_out, xor_41_out, or_66_out);
  not not_58 (not_58_out, A_6[5]);
  and and_106 (and_106_out, xor_42_out, or_58_out);
  and and_107 (and_107_out, A_6[6], B_6[6]);
  or or_52 (or_52_out, A_6[6], B_6[6]);
  not not_59 (not_59_out, A_6[6]);
  and and_108 (and_108_out, xor_43_out, or_60_out);
  not not_60 (not_60_out, A_6[7]);
  and and_109 (and_109_out, xor_44_out, or_61_out);
  and and_110 (and_110_out, A_6[0], B_6[0]);
  or or_53 (or_53_out, A_6[0], B_6[0]);
  xor xor_45 (xor_45_out, xor_37_out, Ci_Sub_2);
  and and_111 (and_111_out, A_6[1], B_6[1]);
  or or_54 (or_54_out, A_6[1], B_6[1]);
  xor xor_46 (xor_46_out, xor_38_out, or_63_out);
  and and_112 (and_112_out, A_6[2], B_6[2]);
  or or_55 (or_55_out, A_6[2], B_6[2]);
  xor xor_47 (xor_47_out, xor_39_out, or_64_out);
  and and_113 (and_113_out, A_6[3], B_6[3]);
  or or_56 (or_56_out, A_6[3], B_6[3]);
  xor xor_48 (xor_48_out, xor_40_out, or_65_out);
  and and_114 (and_114_out, A_6[4], B_6[4]);
  or or_57 (or_57_out, A_6[4], B_6[4]);
  xor xor_49 (xor_49_out, xor_41_out, or_66_out);
  or or_58 (or_58_out, and_105_out, and_97_out);
  and and_115 (and_115_out, A_6[5], B_6[5]);
  or or_59 (or_59_out, A_6[5], B_6[5]);
  xor xor_50 (xor_50_out, xor_42_out, or_58_out);
  or or_60 (or_60_out, and_106_out, and_98_out);
  xor xor_51 (xor_51_out, xor_43_out, or_60_out);
  or or_61 (or_61_out, and_108_out, and_99_out);
  and and_116 (and_116_out, A_6[7], B_6[7]);
  or or_62 (or_62_out, A_6[7], B_6[7]);
  xor xor_52 (xor_52_out, xor_44_out, or_61_out);
  or or_63 (or_63_out, and_101_out, and_93_out);
  or or_64 (or_64_out, and_102_out, and_94_out);
  or or_65 (or_65_out, and_103_out, and_95_out);
  or or_66 (or_66_out, and_104_out, and_96_out);
  or or_67 (Ci_1_3, and_109_out, and_100_out);
  not not_61 (not_61_out, A_6[0]);
  not not_62 (not_62_out, B_6[0]);
  not not_63 (not_63_out, A_6[1]);
  not not_64 (not_64_out, B_6[1]);
  not not_65 (not_65_out, A_6[2]);
  not not_66 (not_66_out, B_6[2]);
  not not_67 (not_67_out, A_6[3]);
  not not_68 (not_68_out, B_6[3]);
  not not_69 (not_69_out, A_6[4]);
  not not_70 (not_70_out, B_6[4]);
  not not_71 (not_71_out, A_6[5]);
  not not_72 (not_72_out, B_6[5]);
  not not_73 (not_73_out, A_6[6]);
  not not_74 (not_74_out, B_6[6]);
  not not_75 (not_75_out, A_6[7]);
  not not_76 (not_76_out, B_6[7]);
  and and_117 (and_117_out, not_61_out, B_6[0]);
  and and_118 (and_118_out, A_6[0], not_62_out);
  and and_119 (and_119_out, not_63_out, B_6[1]);
  and and_120 (and_120_out, A_6[1], not_64_out);
  and and_121 (and_121_out, not_65_out, B_6[2]);
  and and_122 (and_122_out, A_6[2], not_66_out);
  and and_123 (and_123_out, not_67_out, B_6[3]);
  and and_124 (and_124_out, A_6[3], not_68_out);
  and and_125 (and_125_out, not_69_out, B_6[4]);
  and and_126 (and_126_out, A_6[4], not_70_out);
  and and_127 (and_127_out, not_71_out, B_6[5]);
  and and_128 (and_128_out, A_6[5], not_72_out);
  and and_129 (and_129_out, not_73_out, B_6[6]);
  and and_130 (and_130_out, A_6[6], not_74_out);
  and and_131 (and_131_out, not_75_out, B_6[7]);
  and and_132 (and_132_out, A_6[7], not_76_out);
  xor xor_53 (xor_53_out, B_6[4], A_6[4]);
  xor xor_54 (xor_54_out, B_6[5], A_6[5]);
  xor xor_55 (xor_55_out, B_6[6], A_6[6]);
  xor xor_56 (xor_56_out, Ci_Sub, B_3);
  xor xor_57 (xor_57_out, B_6[0], A_6[0]);
  not not_77 (not_77_out, xor_57_out);
  xor xor_58 (xor_58_out, B_6[1], A_6[1]);
  not not_78 (not_78_out, xor_58_out);
  xor xor_59 (xor_59_out, B_6[2], A_6[2]);
  not not_79 (not_79_out, xor_59_out);
  not not_80 (not_80_out, xor_60_out);
  xor xor_60 (xor_60_out, B_6[3], A_6[3]);
  not not_81 (not_81_out, xor_53_out);
  not not_82 (not_82_out, xor_54_out);
  not not_83 (not_83_out, xor_55_out);
  xor xor_61 (xor_61_out, B_6[7], A_6[7]);
  not not_84 (not_84_out, xor_61_out);
  and and_133 (and_133_out, A_3, xor_56_out, xor_56_out);
  xor xor_62 (xor_62_out, A_3, xor_56_out);
  Multiplexer #(.select(3)) multiplexer_11 (
    .in0(and_110_out), .in1(or_53_out), .in2(not_53_out), .in3(xor_45_out), .in4(and_117_out),
    .in5(and_118_out), .in6(not_77_out), .in7(xor_45_out), .out(Salida_2[0]), .sel(OP_4));  // open: en
  Multiplexer #(.select(3)) multiplexer_12 (
    .in0(and_111_out), .in1(or_54_out), .in2(not_54_out), .in3(xor_46_out), .in4(and_119_out),
    .in5(and_120_out), .in6(not_78_out), .in7(xor_46_out), .out(Salida_2[1]), .sel(OP_4));  // open: en
  Multiplexer #(.select(3)) multiplexer_13 (
    .in0(and_112_out), .in1(or_55_out), .in2(not_55_out), .in3(xor_47_out), .in4(and_121_out),
    .in5(and_122_out), .in6(not_79_out), .in7(xor_47_out), .out(Salida_2[2]), .sel(OP_4));  // open: en
  Multiplexer #(.select(3)) multiplexer_14 (
    .in0(and_113_out), .in1(or_56_out), .in2(not_56_out), .in3(xor_48_out), .in4(and_123_out),
    .in5(and_124_out), .in6(not_80_out), .in7(xor_48_out), .out(Salida_2[3]), .sel(OP_4));  // open: en
  Multiplexer #(.select(3)) multiplexer_15 (
    .in0(and_114_out), .in1(or_57_out), .in2(not_57_out), .in3(xor_49_out), .in4(and_125_out),
    .in5(and_126_out), .in6(not_81_out), .in7(xor_49_out), .out(Salida_2[4]), .sel(OP_4));  // open: en
  Multiplexer #(.select(3)) multiplexer_16 (
    .in0(and_115_out), .in1(or_59_out), .in2(not_58_out), .in3(xor_50_out), .in4(and_127_out),
    .in5(and_128_out), .in6(not_82_out), .in7(xor_50_out), .out(Salida_2[5]), .sel(OP_4));  // open: en
  Multiplexer #(.select(3)) multiplexer_17 (
    .in0(and_107_out), .in1(or_52_out), .in2(not_59_out), .in3(xor_51_out), .in4(and_129_out),
    .in5(and_130_out), .in6(not_83_out), .in7(xor_51_out), .out(Salida_2[6]), .sel(OP_4));  // open: en
  Multiplexer #(.select(3)) multiplexer_18 (
    .in0(and_116_out), .in1(or_62_out), .in2(not_60_out), .in3(xor_52_out), .in4(and_131_out),
    .in5(and_132_out), .in6(not_84_out), .in7(xor_52_out), .out(Salida_2[7]), .sel(OP_4));  // open: en
  and and_134 (and_134_out, xor_62_out, Ci_Sub);
  and and_135 (and_135_out, A_3, B_3);
  or or_68 (or_68_out, A_3, B_3);
  not not_85 (not_85_out, A_3);
  xor xor_63 (xor_63_out, xor_62_out, Ci_Sub);
  or or_69 (Ci_1, and_134_out, and_133_out);
  not not_86 (not_86_out, A_3);
  not not_87 (not_87_out, B_3);
  and and_136 (and_136_out, not_86_out, B_3);
  and and_137 (and_137_out, A_3, not_87_out);
  not not_88 (not_88_out, xor_64_out);
  xor xor_64 (xor_64_out, B_3, A_3);
  Multiplexer #(.select(3)) multiplexer_19 (
    .in0(and_135_out), .in1(or_68_out), .in2(not_85_out), .in3(xor_63_out), .in4(and_136_out),
    .in5(and_137_out), .in6(not_88_out), .in7(xor_63_out), .out(S), .sel(OP));  // open: en
  and and_138 (and_141_out[3], A_5[3], B_5[3]);
  Adder #(.width(16)) adder_1 (.a(A_7[15:0]), .b(B_7[15:0]), .out(out_56[15:0]), .cin(in_26), .cout(adder_1_cout));
  Adder #(.width(16)) adder_2 (.a(A_7[31:16]), .b(B_7[31:16]), .out(out_56[31:16]), .cin(adder_1_cout), .cout(out_58));
  and and_139 (and_141_out[2], A_5[2], B_5[3]);
  and and_140 (and_141_out[1], A_5[1], B_5[3]);
  and and_141 (and_141_out[0], A_5[0], B_5[3]);
  and and_142 (and_145_out[3], A_5[3], B_5[2]);
  and and_143 (and_145_out[2], A_5[2], B_5[2]);
  and and_144 (and_145_out[1], A_5[1], B_5[2]);
  and and_145 (and_145_out[0], A_5[0], B_5[2]);
  and and_146 (and_149_out[3], A_5[3], B_5[1]);
  and and_147 (and_149_out[2], A_5[2], B_5[1]);
  and and_148 (and_149_out[1], A_5[1], B_5[1]);
  and and_149 (and_149_out[0], A_5[0], B_5[1]);
  and and_150 (and_152_out[3], A_5[3], B_5[0]);
  and and_151 (and_152_out[2], A_5[2], B_5[0]);
  and and_152 (and_152_out[1], A_5[1], B_5[0]);
  Adder #(.width(4)) adder_3 (
    .a({and_152_out, CERO}), .b(and_149_out), .out({adder_3_cout[2:0], SALIDA_3[1]}), .cout(adder_3_cout[3]));  // open: cin
  Adder #(.width(4)) adder_4 (
    .a(adder_3_cout), .b(and_145_out), .out({adder_4_cout[2:0], SALIDA_3[2]}), .cout(adder_4_cout[3]));  // open: cin
  Adder #(.width(4)) adder_5 (.a(adder_4_cout), .b(and_141_out), .out(SALIDA_3[6:3]), .cout(SALIDA_3[7]));  // open: cin
  and and_153 (SALIDA_3[0], A_5[0], B_5[0]);

  // Notes on the sheet:
  //   HALF ADDER
  //   4.1 ALU de 1 bit
  //   FULL ADDER
  //   Half Adder
  //   4.2 ALU de 8 bits
  //   HALF ADDER
  //   XOR
  //   Full Adder
  //    ALU de 8 bits completo
  //    ALU de 1 bit completo
endmodule
