// Logisim project Practica04.circ as structural Verilog: 5 circuits, main circuit main
module main (
  input  ESCRIBIR,
  input  CI_SUB,
  input  [15:0] ENTRADA,
  output [7:0] RESULTADO,
  output DESBORDAMIENTO
);

  wire [7:0] banco_1_leer_datos_1, banco_1_leer_datos_2, multiplexer_1_out;

  BANCO banco_1 (
    .ESCRIBIR(ESCRIBIR), .ESCRIBIR_DATOS(RESULTADO), .LEER_REGISTRO_1({ENTRADA[10], ENTRADA[11]}),
    .LEER_REGISTRO_2({ENTRADA[8], ENTRADA[9]}), .LEER_DATOS_1(banco_1_leer_datos_1),
    .LEER_DATOS_2(banco_1_leer_datos_2), .ESCRIBIR_REGISTRO({ENTRADA[6], ENTRADA[7]}));
  Multiplexer #(.width(8), .enable("false")) multiplexer_1 (
    .in0(banco_1_leer_datos_1),
    .in1({ENTRADA[0], ENTRADA[1], ENTRADA[2], ENTRADA[3], ENTRADA[4], ENTRADA[5], ENTRADA[6], ENTRADA[7]}),
    .out(multiplexer_1_out), .sel(ENTRADA[12]));
  ALU alu_1 (
    .A(banco_1_leer_datos_2), .Salida(RESULTADO), .OP(ENTRADA[15:13]), .B(multiplexer_1_out),
    .Ci_1(DESBORDAMIENTO), .Ci_Sub(CI_SUB));
endmodule

module ALU (
  input  Ci_Sub,
  input  [2:0] OP,
  input  [7:0] A,
  input  [7:0] B,
  output [7:0] Salida,
  output Ci_1
);

  wire and_1_out, and_2_out, and_3_out, and_4_out, and_5_out, and_6_out, and_7_out, and_8_out, and_9_out,
       and_10_out, and_11_out, and_12_out, and_13_out, and_14_out, and_15_out, and_16_out, and_17_out,
       and_18_out, and_19_out, and_20_out, and_21_out, and_22_out, and_23_out, and_24_out, and_25_out,
       and_26_out, and_27_out, and_28_out, and_29_out, and_30_out, and_31_out, and_32_out, and_33_out,
       and_34_out, and_35_out, and_36_out, and_37_out, and_38_out, and_39_out, and_40_out, not_1_out,
       not_2_out, not_3_out, not_4_out, not_5_out, not_6_out, not_7_out, not_8_out, not_9_out, not_10_out,
       not_11_out, not_12_out, not_13_out, not_14_out, not_15_out, not_16_out, not_17_out, not_18_out,
       not_19_out, not_20_out, not_21_out, not_22_out, not_23_out, not_24_out, not_25_out, not_26_out,
       not_27_out, not_28_out, not_29_out, not_30_out, not_31_out, not_32_out, or_1_out, or_2_out, or_3_out,
       or_4_out, or_5_out, or_6_out, or_7_out, or_8_out, or_9_out, or_10_out, or_11_out, or_12_out,
       or_13_out, or_14_out, or_15_out, xor_1_out, xor_2_out, xor_3_out, xor_4_out, xor_5_out, xor_6_out,
       xor_7_out, xor_8_out, xor_9_out, xor_10_out, xor_11_out, xor_12_out, xor_13_out, xor_14_out,
       xor_15_out, xor_16_out, xor_17_out, xor_18_out, xor_19_out, xor_20_out, xor_21_out, xor_22_out,
       xor_23_out, xor_24_out, xor_25_out, xor_26_out, xor_27_out, xor_28_out, xor_29_out, xor_30_out,
       xor_31_out, xor_32_out;

  xor xor_1 (xor_1_out, Ci_Sub, B[0]);
  xor xor_2 (xor_2_out, Ci_Sub, B[1]);
  xor xor_3 (xor_3_out, Ci_Sub, B[2]);
  xor xor_4 (xor_4_out, Ci_Sub, B[3]);
  xor xor_5 (xor_5_out, Ci_Sub, B[4]);
  xor xor_6 (xor_6_out, Ci_Sub, B[5]);
  xor xor_7 (xor_7_out, Ci_Sub, B[6]);
  xor xor_8 (xor_8_out, Ci_Sub, B[7]);
  and and_1 (and_1_out, A[0], xor_1_out, xor_1_out);
  and and_2 (and_2_out, A[1], xor_2_out, xor_2_out);
  and and_3 (and_3_out, A[2], xor_3_out, xor_3_out);
  and and_4 (and_4_out, A[3], xor_4_out, xor_4_out);
  and and_5 (and_5_out, A[4], xor_5_out, xor_5_out);
  and and_6 (and_6_out, A[5], xor_6_out, xor_6_out);
  and and_7 (and_7_out, A[6], xor_7_out, xor_7_out);
  and and_8 (and_8_out, A[7], xor_8_out, xor_8_out);
  xor xor_9 (xor_9_out, A[0], xor_1_out);
  xor xor_10 (xor_10_out, A[1], xor_2_out);
  xor xor_11 (xor_11_out, A[2], xor_3_out);
  xor xor_12 (xor_12_out, A[3], xor_4_out);
  xor xor_13 (xor_13_out, A[4], xor_5_out);
  xor xor_14 (xor_14_out, A[5], xor_6_out);
  xor xor_15 (xor_15_out, A[6], xor_7_out);
  xor xor_16 (xor_16_out, A[7], xor_8_out);
  and and_9 (and_9_out, xor_15_out, or_14_out);
  and and_10 (and_10_out, A[0], B[0]);
  or or_1 (or_1_out, A[0], B[0]);
  not not_1 (not_1_out, A[0]);
  xor xor_17 (xor_17_out, xor_9_out, Ci_Sub);
  and and_11 (and_11_out, xor_9_out, Ci_Sub);
  and and_12 (and_12_out, A[1], B[1]);
  or or_2 (or_2_out, A[1], B[1]);
  not not_2 (not_2_out, A[1]);
  xor xor_18 (xor_18_out, xor_10_out, or_9_out);
  and and_13 (and_13_out, xor_10_out, or_9_out);
  and and_14 (and_14_out, A[2], B[2]);
  or or_3 (or_3_out, A[2], B[2]);
  not not_3 (not_3_out, A[2]);
  xor xor_19 (xor_19_out, xor_11_out, or_10_out);
  and and_15 (and_15_out, xor_11_out, or_10_out);
  and and_16 (and_16_out, A[3], B[3]);
  or or_4 (or_4_out, A[3], B[3]);
  not not_4 (not_4_out, A[3]);
  xor xor_20 (xor_20_out, xor_12_out, or_11_out);
  and and_17 (and_17_out, xor_12_out, or_11_out);
  and and_18 (and_18_out, A[4], B[4]);
  or or_5 (or_5_out, A[4], B[4]);
  not not_5 (not_5_out, A[4]);
  xor xor_21 (xor_21_out, xor_13_out, or_12_out);
  and and_19 (and_19_out, xor_13_out, or_12_out);
  and and_20 (and_20_out, A[5], B[5]);
  or or_6 (or_6_out, A[5], B[5]);
  not not_6 (not_6_out, A[5]);
  xor xor_22 (xor_22_out, xor_14_out, or_13_out);
  and and_21 (and_21_out, xor_14_out, or_13_out);
  and and_22 (and_22_out, A[6], B[6]);
  or or_7 (or_7_out, A[6], B[6]);
  not not_7 (not_7_out, A[6]);
  xor xor_23 (xor_23_out, xor_15_out, or_14_out);
  and and_23 (and_23_out, A[7], B[7]);
  or or_8 (or_8_out, A[7], B[7]);
  not not_8 (not_8_out, A[7]);
  xor xor_24 (xor_24_out, xor_16_out, or_15_out);
  and and_24 (and_24_out, xor_16_out, or_15_out);
  or or_9 (or_9_out, and_11_out, and_1_out);
  or or_10 (or_10_out, and_13_out, and_2_out);
  or or_11 (or_11_out, and_15_out, and_3_out);
  or or_12 (or_12_out, and_17_out, and_4_out);
  or or_13 (or_13_out, and_19_out, and_5_out);
  or or_14 (or_14_out, and_21_out, and_6_out);
  or or_15 (or_15_out, and_9_out, and_7_out);
  or or_16 (Ci_1, and_24_out, and_8_out);
  not not_9 (not_9_out, A[0]);
  not not_10 (not_10_out, B[0]);
  not not_11 (not_11_out, A[1]);
  not not_12 (not_12_out, B[1]);
  not not_13 (not_13_out, A[2]);
  not not_14 (not_14_out, B[2]);
  not not_15 (not_15_out, A[3]);
  not not_16 (not_16_out, B[3]);
  not not_17 (not_17_out, A[4]);
  not not_18 (not_18_out, B[4]);
  not not_19 (not_19_out, A[5]);
  not not_20 (not_20_out, B[5]);
  not not_21 (not_21_out, A[6]);
  not not_22 (not_22_out, B[6]);
  not not_23 (not_23_out, A[7]);
  not not_24 (not_24_out, B[7]);
  and and_25 (and_25_out, not_9_out, B[0]);
  and and_26 (and_26_out, A[0], not_10_out);
  and and_27 (and_27_out, not_11_out, B[1]);
  and and_28 (and_28_out, A[1], not_12_out);
  and and_29 (and_29_out, not_13_out, B[2]);
  and and_30 (and_30_out, A[2], not_14_out);
  and and_31 (and_31_out, not_15_out, B[3]);
  and and_32 (and_32_out, A[3], not_16_out);
  and and_33 (and_33_out, not_17_out, B[4]);
  and and_34 (and_34_out, A[4], not_18_out);
  and and_35 (and_35_out, not_19_out, B[5]);
  and and_36 (and_36_out, A[5], not_20_out);
  and and_37 (and_37_out, not_21_out, B[6]);
  and and_38 (and_38_out, A[6], not_22_out);
  and and_39 (and_39_out, not_23_out, B[7]);
  and and_40 (and_40_out, A[7], not_24_out);
  xor xor_25 (xor_25_out, B[0], A[0]);
  xor xor_26 (xor_26_out, B[1], A[1]);
  xor xor_27 (xor_27_out, B[2], A[2]);
  xor xor_28 (xor_28_out, B[3], A[3]);
  not not_25 (not_25_out, xor_29_out);
  xor xor_29 (xor_29_out, B[4], A[4]);
  not not_26 (not_26_out, xor_30_out);
  xor xor_30 (xor_30_out, B[5], A[5]);
  xor xor_31 (xor_31_out, B[6], A[6]);
  not not_27 (not_27_out, xor_31_out);
  xor xor_32 (xor_32_out, B[7], A[7]);
  not not_28 (not_28_out, xor_25_out);
  not not_29 (not_29_out, xor_26_out);
  not not_30 (not_30_out, xor_27_out);
  not not_31 (not_31_out, xor_28_out);
  not not_32 (not_32_out, xor_32_out);
  Multiplexer #(.select(3)) multiplexer_1 (
    .in0(and_10_out), .in1(or_1_out), .in2(not_1_out), .in3(xor_17_out), .in4(and_25_out), .in5(and_26_out),
    .in6(not_28_out), .in7(xor_17_out), .out(Salida[0]), .sel(OP));  // open: en
  Multiplexer #(.select(3)) multiplexer_2 (
    .in0(and_12_out), .in1(or_2_out), .in2(not_2_out), .in3(xor_18_out), .in4(and_27_out), .in5(and_28_out),
    .in6(not_29_out), .in7(xor_18_out), .out(Salida[1]), .sel(OP));  // open: en
  Multiplexer #(.select(3)) multiplexer_3 (
    .in0(and_14_out), .in1(or_3_out), .in2(not_3_out), .in3(xor_19_out), .in4(and_29_out), .in5(and_30_out),
    .in6(not_30_out), .in7(xor_19_out), .out(Salida[2]), .sel(OP));  // open: en
  Multiplexer #(.select(3)) multiplexer_4 (
    .in0(and_16_out), .in1(or_4_out), .in2(not_4_out), .in3(xor_20_out), .in4(and_31_out), .in5(and_32_out),
    .in6(not_31_out), .in7(xor_20_out), .out(Salida[3]), .sel(OP));  // open: en
  Multiplexer #(.select(3)) multiplexer_5 (
    .in0(and_18_out), .in1(or_5_out), .in2(not_5_out), .in3(xor_21_out), .in4(and_33_out), .in5(and_34_out),
    .in6(not_25_out), .in7(xor_21_out), .out(Salida[4]), .sel(OP));  // open: en
  Multiplexer #(.select(3)) multiplexer_6 (
    .in0(and_20_out), .in1(or_6_out), .in2(not_6_out), .in3(xor_22_out), .in4(and_35_out), .in5(and_36_out),
    .in6(not_26_out), .in7(xor_22_out), .out(Salida[5]), .sel(OP));  // open: en
  Multiplexer #(.select(3)) multiplexer_7 (
    .in0(and_22_out), .in1(or_7_out), .in2(not_7_out), .in3(xor_23_out), .in4(and_37_out), .in5(and_38_out),
    .in6(not_27_out), .in7(xor_23_out), .out(Salida[6]), .sel(OP));  // open: en
  Multiplexer #(.select(3)) multiplexer_8 (
    .in0(and_23_out), .in1(or_8_out), .in2(not_8_out), .in3(xor_24_out), .in4(and_39_out), .in5(and_40_out),
    .in6(not_32_out), .in7(xor_24_out), .out(Salida[7]), .sel(OP));  // open: en
endmodule

module BANCO (
  input  ESCRIBIR,
  input  [1:0] ESCRIBIR_REGISTRO,
  input  [7:0] ESCRIBIR_DATOS,
  input  [1:0] LEER_REGISTRO_1,
  input  [1:0] LEER_REGISTRO_2,
  output [7:0] LEER_DATOS_1,
  output [7:0] LEER_DATOS_2
);

  wire demultiplexer_2_out0, demultiplexer_2_out1, demultiplexer_2_out2, demultiplexer_2_out3, RELOJ_out;
  wire [7:0] demultiplexer_1_out0, demultiplexer_1_out1, demultiplexer_1_out2, demultiplexer_1_out3,
       registro_1_salida, registro_2_salida, registro_3_salida, registro_4_salida;

  Demultiplexer #(.select(2), .width(8)) demultiplexer_1 (
    .out0(demultiplexer_1_out0), .out1(demultiplexer_1_out1), .out2(demultiplexer_1_out2),
    .out3(demultiplexer_1_out3), .in(ESCRIBIR_DATOS), .sel(ESCRIBIR_REGISTRO));  // open: en
  Clock RELOJ (.out(RELOJ_out));
  Demultiplexer #(.select(2)) demultiplexer_2 (
    .out0(demultiplexer_2_out0), .out1(demultiplexer_2_out1), .out2(demultiplexer_2_out2),
    .out3(demultiplexer_2_out3), .in(ESCRIBIR), .sel(ESCRIBIR_REGISTRO));  // open: en
  registro registro_1 (
    .Entrada(demultiplexer_1_out0), .Salida(registro_1_salida), .Reset(demultiplexer_2_out0), .in_2(RELOJ_out));
  Multiplexer #(.select(2), .width(8)) multiplexer_1 (
    .in0(registro_1_salida), .in1(registro_2_salida), .in2(registro_3_salida), .in3(registro_4_salida),
    .out(LEER_DATOS_1), .sel(LEER_REGISTRO_1));  // open: en
  registro registro_2 (
    .Entrada(demultiplexer_1_out1), .Salida(registro_2_salida), .Reset(demultiplexer_2_out1), .in_2(RELOJ_out));
  registro registro_3 (
    .Entrada(demultiplexer_1_out2), .Salida(registro_3_salida), .Reset(demultiplexer_2_out2), .in_2(RELOJ_out));
  registro registro_4 (
    .Entrada(demultiplexer_1_out3), .Salida(registro_4_salida), .Reset(demultiplexer_2_out3), .in_2(RELOJ_out));
  Multiplexer #(.select(2), .width(8)) multiplexer_2 (
    .in0(registro_1_salida), .in1(registro_2_salida), .in2(registro_3_salida), .in3(registro_4_salida),
    .out(LEER_DATOS_2), .sel(LEER_REGISTRO_2));  // open: en
endmodule

module registro (
  input  Reset,
  input  in_2,
  input  [7:0] Entrada,
  output [7:0] Salida
);

  S_R_Flip_Flop s_r_ff_1 (.S(Entrada[0]), .clk(in_2), .R(Reset), .Q(Salida[0]));  // open: Qn, preset, reset, en
  S_R_Flip_Flop s_r_ff_2 (.S(Entrada[1]), .clk(in_2), .R(Reset), .Q(Salida[1]));  // open: Qn, preset, reset, en
  S_R_Flip_Flop s_r_ff_3 (.S(Entrada[2]), .clk(in_2), .R(Reset), .Q(Salida[2]));  // open: Qn, preset, reset, en
  S_R_Flip_Flop s_r_ff_4 (.S(Entrada[3]), .clk(in_2), .R(Reset), .Q(Salida[3]));  // open: Qn, preset, reset, en
  S_R_Flip_Flop s_r_ff_5 (.S(Entrada[4]), .clk(in_2), .R(Reset), .Q(Salida[4]));  // open: Qn, preset, reset, en
  S_R_Flip_Flop s_r_ff_6 (.S(Entrada[5]), .clk(in_2), .R(Reset), .Q(Salida[5]));  // open: Qn, preset, reset, en
  S_R_Flip_Flop s_r_ff_7 (.S(Entrada[6]), .clk(in_2), .R(Reset), .Q(Salida[6]));  // open: Qn, preset, reset, en
  S_R_Flip_Flop s_r_ff_8 (.S(Entrada[7]), .clk(in_2), .R(Reset), .Q(Salida[7]));  // open: Qn, preset, reset, en
endmodule

module AUTOMATA (
  input  i,
  input  in_2
);

  wire and_1_out, and_2_out, and_3_out, and_4_out, clock_1_out, j_k_ff_1_q, j_k_ff_2_q, not_1_out, not_2_out,
       not_3_out, not_4_out, or_1_out, or_2_out;

  not not_1 (not_1_out, j_k_ff_2_q);
  not not_2 (not_2_out, j_k_ff_1_q);
  and and_1 (and_1_out, j_k_ff_1_q, not_1_out);
  and and_2 (and_2_out, not_2_out, j_k_ff_2_q);
  and and_3 (and_3_out, i, j_k_ff_2_q);
  not not_3 (not_3_out, i);
  not not_4 (not_4_out, j_k_ff_2_q);
  or or_1 (or_1_out, and_1_out, and_2_out);
  and and_4 (and_4_out, not_3_out, not_4_out);
  or or_2 (or_2_out, and_3_out, and_4_out);
  Clock clock_1 (.out(clock_1_out));
  J_K_Flip_Flop j_k_ff_1 (.J(or_2_out), .clk(clock_1_out), .K(in_2), .Q(j_k_ff_1_q));  // open: Qn, preset, en, reset
  J_K_Flip_Flop j_k_ff_2 (.J(or_1_out), .clk(clock_1_out), .K(in_2), .Q(j_k_ff_2_q));  // open: Qn, preset, en, reset

  // Notes on the sheet:
  //   S0
  //   S1
  //   S0+
  //   S1+
endmodule
